# Fritzing sketch simpefan (saved by Fritzing 0.9.2b)
breadboards: 1

parts:
  Power_Supply = DC Power [voltage=12V]
  Fan_2 = DC Motor
  Fan_1 = DC Motor

nets:
  N1: Power_Supply.V+, Fan_2.pin_2, Fan_1.pin_2
  N2: Power_Supply.V-, Fan_2.pin_1, Fan_1.pin_1
